# Fritzing sketch snatchpad (saved by Fritzing 0.9.9b)

parts:
  Part1 = Arduino Pro Micro (Clone)
  2_2 = Rotary Encoder [package=THT]
  2_0 = Rotary Encoder [package=THT]
  D1 = Diode [package=diode-1n4148]
  D2 = Diode [package=diode-1n4148]
  D3 = Diode [package=diode-1n4148]
  D4 = Diode [package=diode-1n4148]
  D5 = Diode [package=diode-1n4148]
  D6 = Diode [package=diode-1n4148]
  D7 = Diode [package=diode-1n4148]
  D8 = Diode [package=diode-1n4148]
  0_0 = Round Pushbutton
  0_1 = Round Pushbutton
  0_2 = Round Pushbutton
  1_2 = Round Pushbutton
  0_1_2 = Round Pushbutton
  0_0_2 = Round Pushbutton

nets:
  N1: Part1.TXO, 2_0.EncoderPinB
  N2: Part1.RXI, 2_0.EncoderPinA
  N3: Part1.GND, 2_2.EncoderPinC, 2_0.EncoderPinC
  N4: Part1.D2, 2_2.EncoderPinA
  N5: Part1.D3, 2_2.EncoderPinB
  N6: Part1.D16, 2_2.SwitchPinE, 0_2.leg1
  N7: Part1.D14, 0_1.leg1, 0_1_2.leg1
  N8: Part1.D15, 2_0.SwitchrPinD, 0_0.leg1
  N9: Part1.A1, D7.C, D8.C
  N10: Part1.A2, D3.C
  N11: Part1.A3, D4.C
  N12: 2_2.SwitchrPinD, D7.A
  N13: 2_0.SwitchPinE, D8.A
  N14: D1.A, 0_0.leg0
  N15: D1.C, D2.A, 0_1.leg0
  N16: D2.C, D4.A, 0_2.leg0
  N17: D3.A, D5.C, 1_2.leg0
  N18: D5.A, D6.C, 0_1_2.leg0
  N19: D6.A, 0_0_2.leg0

notes:
  EC11 pins
  A = Red
  B = Green
  Ground = Black

custom parts:
  Rotary Encoder: Rotary Encoder from ALPSec11e with switch.
